# Fritzing sketch iot_button_wemos (saved by Fritzing 0.9.3b)
circuit board: 5.23177cm x 2.93254cm
stripboards: 1

parts:
  WeMos_D1_Mini1 = WeMos D1 Mini
  U1 = LIPO-110mAh [package=lipo-110]
  S1 = Pushbutton [package="[SMD]"]

nets:
  N1: WeMos_D1_Mini1.3V3, S1.Pin_3, S1.Pin_4
  N2: WeMos_D1_Mini1.5V, U1.+
  N3: WeMos_D1_Mini1.D8, S1.Pin_1, S1.Pin_2
  N4: WeMos_D1_Mini1.G, U1.-
