# Fritzing sketch iot_button_wemos (saved by Fritzing 0.9.3b)

parts:
  WeMos_D1_Mini1 = WeMos D1 Mini
  U1 = LIPO-110mAh [package=lipo-110]
  S1 = Momentary Switch [package=ksa_sealed_tac_switch]
  LED1 = RGB LED (com. cathode, rgb) [package="5 mm [THT]"]  # not connected

nets:
  N1: WeMos_D1_Mini1.3V3, S1.4
  N2: WeMos_D1_Mini1.5V, U1.+
  N3: WeMos_D1_Mini1.D8, S1.2
  N4: WeMos_D1_Mini1.G, U1.-
